# Fritzing sketch Termometer (saved by Fritzing 0.9.2b)

parts:
  Part1 = Arduino Uno (Rev3)
  S1 = Pushbutton [package="[THT]"]
  S2 = Pushbutton [package="[THT]"]
  LCD1 = LCD screen
  T1 = LM34 Temperature Sensor [package="TO92 [THT]"]
  R1 = Resistor [tolerance=±5% resistance=10k package=THT]  # not connected
  R2 = Resistor [tolerance=±5% resistance=10k package=THT]  # not connected
  J1 = Piezo Speaker
  R3 = Resistor [tolerance=±5% resistance=1k package=THT]

nets:
  N1: Part1.A0, S1.Pin_4
  N2: Part1.A1, S2.Pin_3, S2.Pin_4
  N3: Part1.A4/SDA, LCD1.DB1
  N4: Part1.A5/SCL, LCD1.DB0
  N5: Part1.D2, T1.Vout
  N6: Part1.D3_PWM, J1.pin2
  N7: Part1.5V, LCD1.LED+
  N8: Part1.GND, LCD1.LED-
  N9: T1.+Vs, R3.Pin_1

notes:
  SDA
  SCL
