# Fritzing sketch Termometer_breadboard (saved by Fritzing 0.9.2b)
breadboards: 1

parts:
  Part1 = Arduino Uno (Rev3)
  S1 = Pushbutton [package="[THT]"]
  S2 = Pushbutton [package="[THT]"]
  LCD1 = LCD screen
  T1 = LM34 Temperature Sensor [package="TO92 [THT]"]
  R2 = Resistor [tolerance=±5% resistance=10k package=THT]
  J1 = Piezo Speaker
  R3 = Resistor [tolerance=±5% resistance=220 package=THT]
  R4 = Resistor [tolerance=±5% resistance=10k package=THT]

nets:
  N1: Part1.A0, S1.Pin_1, S1.Pin_2, R2.Pin_1
  N2: Part1.A1, S2.Pin_1, S2.Pin_2, R4.Pin_1
  N3: Part1.A4/SDA, LCD1.DB1
  N4: Part1.A5/SCL, LCD1.DB0
  N5: Part1.D2, T1.Vout, R3.Pin_1
  N6: Part1.D3_PWM, J1.pin2
  N7: Part1.5V, S1.Pin_3, S1.Pin_4, S2.Pin_3, S2.Pin_4, LCD1.LED+, T1.+Vs, R3.Pin_0
  GND: Part1.GND, LCD1.LED-, T1.GND, R2.Pin_0, J1.pin1, R4.Pin_0
